// Logisim project 7.circ as structural Verilog: 1 circuit, main circuit main
module main (
  input  A,
  input  B,
  output Sum,
  output carry
);

  xor xor_1 (Sum, A, B);
  and and_1 (carry, A, B);
endmodule
